# Fritzing sketch nano_button_potentiometer (saved by Fritzing 0.9.4)
breadboards: 1

parts:
  S1 = Pushbutton [package="[SMD]"]
  U1 = POT [package=alps_pot]
  Part1 = Arduino Nano 33 IoT

nets:
  N1: S1.Pin_1, S1.Pin_2, U1.A, Part1.GND
  N2: S1.Pin_3, S1.Pin_4, Part1.D2
  N3: U1.E, Part1.3V3
  N4: U1.S, Part1.A0

custom parts:
  Arduino Nano 33 IoT: The Arduino Nano 33 IoT is a small, complete, and breadboard-friendly board based on the Arm® Cortex®-M0 32-bit SAMD21. It has onboard WiFi and Bluetooth® connectivity through a u-blox NINA-W10 chipset. Secure communication is ensured through the Microchip® ECC608 crypto chip. It also has 6-axis LSM6DS3 IMU.
